# Fritzing sketch connections (saved by Fritzing 0.9.3b)

parts:
  U1 = NodeMCU V3.0
  S1 = SWITCH-MOMENTARY-2 [package=reed_switch_plastic]
  R1 = Resistor [tolerance=±5% resistance=75k package=THT]

nets:
  N1: U1.D6, S1.1, R1.Pin_0
  N2: U1.GND, S1.2

notes:
  DOOR SENSOR
  75K
  Door sensor

custom parts:
  NodeMCU V3.0: ESP8266 based NodeMCU
