# Fritzing sketch connections (saved by Fritzing 0.9.3b)

parts:
  TP1 = TP4056 [chip_label=TP4056 package="DIP (Dual Inline) [THT]"]
  U1 = NodeMCU V3.0
  D1 = Schottky Diode [part_number=1N5817 package="300 mil [THT]"]
  D2 = Schottky Diode [part_number=1N5817 package="300 mil [THT]"]
  S1 = SWITCH-MOMENTARY-2 [package=reed_switch_plastic]
  U3 = LIPO-2000mAh [package=lipo-2000]
  JS1 = Generic Jumper Shunt
  R1 = Resistor [tolerance=±5% resistance=470 package=THT]
  R2 = Resistor [tolerance=±5% resistance=12M package=THT]

nets:
  N1: TP1.pin1, D1.anode
  N2: TP1.pin3, D2.anode
  N3: TP1.pin4, U3.+
  N4: TP1.pin5, U3.-
  GND: TP1.pin6, U1.TX, U1.GND, U1.Vin, D1.cathode, S1.1
  N5: U1.D0, U1.D1, JS1.pin1
  N6: U1.D6, R2.Pin_1
  N7: U1.3V3, D2.cathode
  N8: U1.RST, JS1.pin2, R1.Pin_0, R2.Pin_0
  N9: S1.2, R1.Pin_1

notes:
  DOOR SENSOR
  CHARGER CIRCUIT
  BATTERY
  DIODE
  470R
  12M
  JUMPER
  (remove to write new FW)
  Tp4056

custom parts:
  TP4056: A DIP stand-in part for whatever IC you want. With 6 pins on a 300mil dual inline package (DIP) footprint.
  NodeMCU V3.0: ESP8266 based NodeMCU
